// Logisim project lab 4 4.circ as structural Verilog: 1 circuit, main circuit main
module main (
  input  a,
  input  b,
  input  c,
  input  d,
  output w,
  output x,
  output Y,
  output Z
);

  wire nand_1_out, nand_2_out, nand_3_out, nand_4_out, nand_5_out, nand_6_out, nand_7_out, nand_8_out,
       not_1_out, not_2_out, not_3_out;

  not not_1 (not_1_out, a);
  not not_2 (not_2_out, b);
  not not_3 (not_3_out, c);
  not not_4 (Z, d);
  nand nand_1 (nand_1_out, b, not_3_out, Z);
  nand nand_2 (nand_2_out, b, d);
  nand nand_3 (nand_3_out, b, c);
  nand nand_4 (nand_4_out, a, a);
  nand nand_5 (nand_5_out, not_2_out, d);
  nand nand_6 (nand_6_out, not_2_out, c);
  nand nand_7 (nand_7_out, not_3_out, Z);
  nand nand_8 (nand_8_out, c, d);
  nand nand_9 (w, nand_2_out, nand_3_out, nand_4_out);
  nand nand_10 (x, nand_1_out, nand_5_out, nand_6_out);
  nand nand_11 (Y, nand_7_out, nand_8_out);
endmodule
